# Fritzing sketch 4N36_LedTesterApp (saved by Fritzing 1.0.6)
breadboards: 1

parts:
  U1 = Optocoupler [package=THT]
  esp1 = ESP32 DevKitc V4
  R1 = Resistor [tolerance=±5% power=0.25W resistance=220 package=THT]
  LED1 = LED - 5mm [color="Red (633nm)" current=0.030A package="5 mm [THT]"]
  R2 = Resistor [tolerance=±5% power=0.25W resistance=470 package=THT]
  Part1 = Lilypad Power Supply

nets:
  N1: U1.Pin_1, R2.Pin_1
  N2: U1.Pin_2, esp1.GND#32
  N3: U1.Pin_4, R1.Pin_0, Part1.GND
  N4: U1.Pin_5, LED1.cathode
  N5: esp1.IO25, R2.Pin_0
  N6: R1.Pin_1, LED1.anode

custom parts:
  ESP32 DevKitc V4: ESP32-DevKitC board with ESP32-WROOM-32 module. ESP32-DevKitC V4 is a small-sized ESP32-based development board produced by Espressif. Most of the pins on the ESP module are broken out to the pin headers on the board. The pins D0, D1, D2, D3, CMD and CLK are used internally for communication between ESP32 and SPI flash memory. They are grouped on both sides near the USB connector. Avoid using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
